// Logisim project LivresDesCompsants-DESKTOP-A4BDADO.circ as structural Verilog
module main (
);

  QuatreAUnCompresseurEW quatreauncompresseurew_1 ();  // open: OROLOGE, COMMENCER, A0, A1, A2, A3, FINI, A
  UnAQuatreDecompresseurEW unaquatredecompresseurew_1 ();  // open: OROLOGE, COMMENCER, A, A0, A1, A2, FINI, A3
  QuatreAUnCompresseurNS quatreauncompresseurns_1 ();  // open: OROLOGE, COMMENCER, A0, A1, A2, A3, FINI, A
  UnAQuatreDecompresseurNS unaquatredecompresseurns_1 ();  // open: OROLOGE, COMMENCER, A, A0, A1, A2, A3, FINI
  ZeroATroisIncremAjoutantEW zeroatroisincremajoutantew_1 ();  // open: CMR, OROLOGE, COMMENCER, in_3, in_1, FINI, out_6, out_7, S0, S1
  OneBitAjoutantEW onebitajoutantew_1 ();  // open: A, B, Cin, ACT, K, Cout
  ZeroATroisIncremAjoutantNS zeroatroisincremajoutantns_1 ();  // open: OROLOGE, COMMENCER, FINI, S0, S1
  OneBitAjoutantNS onebitajoutantns_1 ();  // open: A, B, Cin, ACT, K, Cout
  QuatreBitAjoutantEW quatrebitajoutantew_1 ();  // open: B, A, HORG, CMR, Cin, RE, RST, FINI, K0, K1, K2, K3
endmodule

module QuatreAUnCompresseurEW (
  input  A0,
  input  A1,
  input  A2,
  input  A3,
  input  OROLOGE,
  input  COMMENCER,
  output FINI,
  output A
);

  wire [1:0] zeroatroisincremajoutantew_1_s0;

  Multiplexer #(.select(2)) multiplexer_1 (
    .in0(A0), .in1(A1), .in2(A2), .in3(A3), .out(A), .sel(zeroatroisincremajoutantew_1_s0));
  ZeroATroisIncremAjoutantEW zeroatroisincremajoutantew_1 (
    .OROLOGE(OROLOGE), .COMMENCER(COMMENCER), .FINI(FINI), .S0(zeroatroisincremajoutantew_1_s0[0]),
    .S1(zeroatroisincremajoutantew_1_s0[1]));  // open: CMR, in_3, in_1, out_6, out_7

  // Notes on the sheet:
  //   on utilise "fini" bit avec la dernière bit pour minimaliser le delai des components sous-nivel
  //   le delai (pour ejemple un delai d'un cycle peut faire dans les components seuls qu'ont besoin de ça
endmodule

module QuatreAUnCompresseurNS (
  input  A0,
  input  A1,
  input  A2,
  input  A3,
  input  OROLOGE,
  input  COMMENCER,
  output FINI,
  output A
);

  wire [1:0] zeroatroisincremajoutantew_1_s0;

  Multiplexer #(.select(2)) multiplexer_1 (
    .in0(A0), .in1(A1), .in2(A2), .in3(A3), .out(A), .sel(zeroatroisincremajoutantew_1_s0));
  ZeroATroisIncremAjoutantEW zeroatroisincremajoutantew_1 (
    .OROLOGE(OROLOGE), .COMMENCER(COMMENCER), .FINI(FINI), .S0(zeroatroisincremajoutantew_1_s0[0]),
    .S1(zeroatroisincremajoutantew_1_s0[1]));  // open: CMR, in_3, in_1, out_6, out_7

  // Notes on the sheet:
  //   c'est la même sauf qu'il va du nord au sud
endmodule

module UnAQuatreDecompresseurEW (
  input  OROLOGE,
  input  COMMENCER,
  input  A,
  output FINI,
  output A0,
  output A1,
  output A2,
  output A3
);

  wire [1:0] zeroatroisincremajoutantns_1_s0;

  ZeroATroisIncremAjoutantNS zeroatroisincremajoutantns_1 (
    .OROLOGE(OROLOGE), .COMMENCER(COMMENCER), .FINI(FINI), .S0(zeroatroisincremajoutantns_1_s0[0]),
    .S1(zeroatroisincremajoutantns_1_s0[1]));
  Demultiplexer #(.select(2)) demultiplexer_1 (
    .out0(A0), .out1(A1), .out2(A2), .out3(A3), .in(A), .sel(zeroatroisincremajoutantns_1_s0));
endmodule

module UnAQuatreDecompresseurNS (
  input  OROLOGE,
  input  COMMENCER,
  input  A,
  output FINI,
  output A0,
  output A1,
  output A2,
  output A3
);

  wire [1:0] zeroatroisincremajoutantns_1_s0;

  ZeroATroisIncremAjoutantNS zeroatroisincremajoutantns_1 (
    .OROLOGE(OROLOGE), .COMMENCER(COMMENCER), .FINI(FINI), .S0(zeroatroisincremajoutantns_1_s0[0]),
    .S1(zeroatroisincremajoutantns_1_s0[1]));
  Demultiplexer #(.select(2)) demultiplexer_1 (
    .out0(A0), .out1(A1), .out2(A2), .out3(A3), .in(A), .sel(zeroatroisincremajoutantns_1_s0));
endmodule

module ZeroATroisIncremAjoutantEW (
  input  in_1,
  input  CMR,
  input  in_3,
  input  OROLOGE,
  input  COMMENCER,
  output out_6,
  output out_7,
  output S0,
  output S1,
  output FINI
);

  wire and_2_out, d_ff_1_q, nand_1_out, or_1_out, t_ff_1_q;

  S_R_Flip_Flop s_r_ff_1 ();  // open: S, R, clk, Q, reset, Qn, preset
  J_K_Flip_Flop j_k_ff_1 (.J(in_1), .K(in_1), .clk(in_3), .Q(out_6));  // open: Qn, preset, reset
  and and_1 (FINI, S1, S0);
  T_Flip_Flop t_ff_1 (.T(or_1_out), .clk(OROLOGE), .Q(t_ff_1_q));  // open: Qn, reset, preset
  or or_1 (or_1_out, FINI, COMMENCER);
  J_K_Flip_Flop j_k_ff_2 (.J(out_6), .K(out_6), .clk(in_3), .Q(out_7));  // open: Qn, preset, reset
  D_Flip_Flop d_ff_1 (.D(nand_1_out), .clk(and_2_out), .Q(d_ff_1_q));  // open: Qn, preset, reset
  and and_2 (and_2_out, OROLOGE, t_ff_1_q);
  J_K_Flip_Flop j_k_ff_3 (.J(d_ff_1_q), .K(d_ff_1_q), .clk(and_2_out), .Q(S0));  // open: Qn, preset, reset
  nand nand_1 (nand_1_out, S0, S1);
  J_K_Flip_Flop j_k_ff_4 (.J(S0), .K(S0), .clk(and_2_out), .Q(S1));  // open: Qn, preset, reset

  // Notes on the sheet:
  //   un formation JK simple, qui utilise un DFF pour un 1-cycle delai
  //   avec ça, il lit 00 pour un temps et n'est pas incrémenter instantement de "00" à "01"
  //   le commencer (cmr) bit peut être activé pour tout le temps petit ou grand
  //   mais, le cmr bit regarde le status pour un cycle trop long
  //   c'est NAND gate fait le 1-temps delai
endmodule

module ZeroATroisIncremAjoutantNS (
  input  OROLOGE,
  input  COMMENCER,
  output S0,
  output S1,
  output FINI
);

  wire and_2_out, d_ff_1_q, nand_1_out, or_1_out, t_ff_1_q;

  and and_1 (FINI, S1, S0);
  T_Flip_Flop t_ff_1 (.T(or_1_out), .clk(OROLOGE), .Q(t_ff_1_q));  // open: Qn, reset, preset
  or or_1 (or_1_out, FINI, COMMENCER);
  D_Flip_Flop d_ff_1 (.D(nand_1_out), .clk(and_2_out), .Q(d_ff_1_q));  // open: Qn, preset, reset
  and and_2 (and_2_out, OROLOGE, t_ff_1_q);
  J_K_Flip_Flop j_k_ff_1 (.J(d_ff_1_q), .K(d_ff_1_q), .clk(and_2_out), .Q(S0));  // open: Qn, preset, reset
  nand nand_1 (nand_1_out, S0, S1);
  J_K_Flip_Flop j_k_ff_2 (.J(S0), .K(S0), .clk(and_2_out), .Q(S1));  // open: Qn, preset, reset
endmodule

module OneBitAjoutantEW (
  input  A,
  input  B,
  input  Cin,
  input  ACT,
  output Cout,
  output K
);

  wire and_1_out, and_2_out, or_1_out, xor_1_out, xor_2_out;

  xor xor_1 (xor_1_out, A, B);
  and and_1 (and_1_out, A, B);
  and and_2 (and_2_out, xor_1_out, Cin);
  xor xor_2 (xor_2_out, xor_1_out, Cin);
  or or_1 (or_1_out, and_1_out, and_2_out);
  and and_3 (K, xor_2_out, ACT);
  and and_4 (Cout, or_1_out, ACT);

  // Notes on the sheet:
  //   1-bit tout ajoutant
  //   L'Inclusion de l'Activer est étrange mais, c'est similaire de "commencer" dans tous autres compsants
endmodule

module OneBitAjoutantNS (
  input  A,
  input  B,
  input  Cin,
  input  ACT,
  output Cout,
  output K
);

  wire and_1_out, and_2_out, or_1_out, xor_1_out, xor_2_out;

  xor xor_1 (xor_1_out, A, B);
  and and_1 (and_1_out, A, B);
  and and_2 (and_2_out, xor_1_out, Cin);
  xor xor_2 (xor_2_out, xor_1_out, Cin);
  or or_1 (or_1_out, and_1_out, and_2_out);
  and and_3 (K, xor_2_out, ACT);
  and and_4 (Cout, or_1_out, ACT);

  // Notes on the sheet:
  //   le NS du tout ajoutant
endmodule

module QuatreBitAjoutantEW (
  input  [3:0] A,
  input  HORG,
  input  CMR,
  input  [3:0] B,
  input  RE,
  input  RST,
  input  Cin,
  output FINI,
  output K0,
  output K1,
  output K2,
  output K3
);

  wire Decompresseur_a, OneBitAjoutant_cout, OneBitAjoutant_k, or_1_out, quatreauncompresseurew_1_a;

  QuatreAUnCompresseurEW Decompresseur (
    .OROLOGE(HORG), .COMMENCER(CMR), .A0(A[0]), .A1(A[1]), .A2(A[2]), .A3(A[3]), .FINI(FINI),
    .A(Decompresseur_a));
  QuatreAUnCompresseurEW quatreauncompresseurew_1 (
    .OROLOGE(HORG), .COMMENCER(CMR), .A0(B[0]), .A1(B[1]), .A2(B[2]), .A3(B[3]),
    .A(quatreauncompresseurew_1_a));  // open: FINI
  or or_1 (or_1_out, Cin, OneBitAjoutant_cout);
  OneBitAjoutantEW OneBitAjoutant (
    .A(Decompresseur_a), .B(quatreauncompresseurew_1_a), .Cin(or_1_out), .ACT(HORG), .K(OneBitAjoutant_k),
    .Cout(OneBitAjoutant_cout));
  SerialeParalelleRegistreEW Memoire (
    .OROLOGE(HORG), .COMMENCER(CMR), .ENTREE(OneBitAjoutant_k), .RST(RST), .LIRE_ENABLE(RE), .D0(K0),
    .D1(K1), .D2(K2), .D3(K3));  // open: FINI

  // Notes on the sheet:
  //   je ne sais pas la raison que ce truc garde des values et nes autres
  //   ie A = 4, B = 8, fait 12
  //   mais M1 est 1 tous temps, et M2 changer entre 0 et 1
endmodule

module souvenir (
  input  OROLOGE,
  input  COMMENCER,
  input  Entree,
  input  RST,
  output M0,
  output M1,
  output M2,
  output M3
);

  wire d_ff_1_q, d_ff_2_q, d_ff_3_q, d_ff_4_q, demultiplexer_1_out0, demultiplexer_1_out1,
       demultiplexer_1_out2, demultiplexer_1_out3, nand_1_out, nand_2_out, nand_3_out, nand_4_out, not_1_out,
       not_2_out, zeroatroisincremajoutantns_1_fini;
  wire [1:0] zeroatroisincremajoutantns_1_s0;

  not not_1 (not_1_out, zeroatroisincremajoutantns_1_s0[0]);
  not not_2 (not_2_out, zeroatroisincremajoutantns_1_s0[1]);
  Demultiplexer #(.select(2)) demultiplexer_1 (
    .out0(demultiplexer_1_out0), .out1(demultiplexer_1_out1), .out2(demultiplexer_1_out2),
    .out3(demultiplexer_1_out3), .in(Entree), .sel(zeroatroisincremajoutantns_1_s0));
  ZeroATroisIncremAjoutantNS zeroatroisincremajoutantns_1 (
    .OROLOGE(OROLOGE), .COMMENCER(COMMENCER), .FINI(zeroatroisincremajoutantns_1_fini),
    .S0(zeroatroisincremajoutantns_1_s0[0]), .S1(zeroatroisincremajoutantns_1_s0[1]));
  D_Flip_Flop #(.trigger("low")) d_ff_1 (
    .D(demultiplexer_1_out0), .clk(nand_1_out), .Q(d_ff_1_q), .reset(RST));  // open: Qn, preset
  nand nand_1 (nand_1_out, not_1_out, not_2_out);
  D_Flip_Flop #(.trigger("low")) d_ff_2 (
    .D(demultiplexer_1_out1), .clk(nand_2_out), .Q(d_ff_2_q), .reset(RST));  // open: Qn, preset
  nand nand_2 (nand_2_out, not_2_out, zeroatroisincremajoutantns_1_s0[0]);
  D_Flip_Flop #(.trigger("low")) d_ff_3 (
    .D(demultiplexer_1_out2), .clk(nand_3_out), .Q(d_ff_3_q), .reset(RST));  // open: Qn, preset
  nand nand_3 (nand_3_out, zeroatroisincremajoutantns_1_s0[1], not_1_out);
  D_Flip_Flop #(.trigger("low")) d_ff_4 (
    .D(demultiplexer_1_out3), .clk(nand_4_out), .Q(d_ff_4_q), .reset(RST));  // open: Qn, preset
  nand nand_4 (nand_4_out, zeroatroisincremajoutantns_1_s0[0], zeroatroisincremajoutantns_1_s0[1]);
  D_Flip_Flop d_ff_5 (.D(d_ff_1_q), .clk(zeroatroisincremajoutantns_1_fini), .Q(M0), .reset(RST));  // open: Qn, preset
  D_Flip_Flop d_ff_6 (.D(d_ff_2_q), .clk(zeroatroisincremajoutantns_1_fini), .Q(M1), .reset(RST));  // open: Qn, preset
  D_Flip_Flop d_ff_7 (.D(d_ff_3_q), .clk(zeroatroisincremajoutantns_1_fini), .Q(M2), .reset(RST));  // open: Qn, preset
  D_Flip_Flop d_ff_8 (.D(d_ff_4_q), .clk(zeroatroisincremajoutantns_1_fini), .Q(M3), .reset(RST));  // open: Qn, preset

  // Notes on the sheet:
  //   les choses ci-dessus sont essentiellement un Demux lol 
  //   je les corrigerai plus tard
  //   N'est pas utilisant
  //   M0
  //   M1
  //   M2
  //   M3
  //   4-1 single flush single save unit de mémoire
endmodule

module SerialeParalelleRegistreEW (
  input  ENTREE,
  input  OROLOGE,
  input  COMMENCER,
  input  RST,
  input  LIRE_ENABLE,
  output D0,
  output D1,
  output D2,
  output FINI,
  output D3
);

  wire d_ff_1_q, d_ff_2_q, d_ff_3_q, d_ff_4_q, demultiplexer_1_out0, demultiplexer_1_out1,
       demultiplexer_1_out2, demultiplexer_1_out3, demultiplexer_2_out0, demultiplexer_2_out1,
       demultiplexer_2_out2, demultiplexer_2_out3;
  wire [1:0] zeroatroisincremajoutantew_1_s0;

  Demultiplexer #(.select(2)) demultiplexer_1 (
    .out0(demultiplexer_1_out0), .out1(demultiplexer_1_out1), .out2(demultiplexer_1_out2),
    .out3(demultiplexer_1_out3), .in(ENTREE), .sel(zeroatroisincremajoutantew_1_s0));
  Demultiplexer #(.select(2)) demultiplexer_2 (
    .out0(demultiplexer_2_out0), .out1(demultiplexer_2_out1), .out2(demultiplexer_2_out2),
    .out3(demultiplexer_2_out3), .in(1'b1), .sel(zeroatroisincremajoutantew_1_s0));
  ZeroATroisIncremAjoutantEW zeroatroisincremajoutantew_1 (
    .OROLOGE(OROLOGE), .COMMENCER(COMMENCER), .FINI(FINI), .S0(zeroatroisincremajoutantew_1_s0[0]),
    .S1(zeroatroisincremajoutantew_1_s0[1]));  // open: CMR, in_3, in_1, out_6, out_7
  D_Flip_Flop #(.trigger("high")) d_ff_1 (
    .D(demultiplexer_1_out0), .clk(demultiplexer_2_out0), .Q(d_ff_1_q), .reset(RST));  // open: Qn, preset
  D_Flip_Flop d_ff_2 (
    .D(demultiplexer_1_out1), .clk(demultiplexer_2_out1), .Q(d_ff_2_q), .reset(RST));  // open: Qn, preset
  D_Flip_Flop d_ff_3 (
    .D(demultiplexer_1_out2), .clk(demultiplexer_2_out2), .Q(d_ff_3_q), .reset(RST));  // open: Qn, preset
  D_Flip_Flop d_ff_4 (
    .D(demultiplexer_1_out3), .clk(demultiplexer_2_out3), .Q(d_ff_4_q), .reset(RST));  // open: Qn, preset
  assign D0 = LIRE_ENABLE ? d_ff_1_q : 1'bz;  // Controlled_Buffer controlled_buffer_1
  assign D1 = LIRE_ENABLE ? d_ff_2_q : 1'bz;  // Controlled_Buffer controlled_buffer_2
  assign D2 = LIRE_ENABLE ? d_ff_3_q : 1'bz;  // Controlled_Buffer controlled_buffer_3
  assign D3 = LIRE_ENABLE ? d_ff_4_q : 1'bz;  // Controlled_Buffer controlled_buffer_4

  // Notes on the sheet:
  //   utilisant les deux DEMUXs en lieu d'un NAND network
  //   Sériale Entrée -> Paralelle Sortie
  //   4-1 single flush, single save unit de mémoire
endmodule

module ALU (
  input  [3:0] A,
  input  [2:0] OP_CODE,
  input  [3:0] B
);

  wire [3:0] demultiplexer_1_out0, demultiplexer_2_out0;

  Demultiplexer #(.select(3), .width(4)) demultiplexer_1 (
    .out0(demultiplexer_1_out0), .in(A), .sel(OP_CODE));  // open: out1, out2, out3, out4, out5, out6, out7
  Demultiplexer #(.select(3), .width(4)) demultiplexer_2 (
    .out0(demultiplexer_2_out0), .in(B), .sel(OP_CODE));  // open: out1, out2, out3, out4, out5, out6, out7
  QuatreBitAjoutantEW quatrebitajoutantew_1 (
    .B(demultiplexer_2_out0), .A(demultiplexer_1_out0));  // open: HORG, CMR, Cin, RE, RST, FINI, K0, K1, K2, K3

  // Notes on the sheet:
  //   Ajoutant - 00
  //   Subtracteur - 01
  //   OR Logique - 02
  //   Ajoutant, Subtracteur, OR Logique, AND Logique, SRL, SLL, 2s Comp, 1s Comp
endmodule

module DeuxCompEW (
  input  [3:0] A,
  input  in_2,
  input  OROLOGE,
  input  COMMENCER,
  output out_5
);

  QuatreBitAjoutantEW quatrebitajoutantew_1 (
    .B(A), .A(4'b0001), .HORG(OROLOGE), .CMR(COMMENCER), .Cin(in_2), .RST(out_5));  // open: RE, FINI, K0, K1, K2, K3
endmodule

module ProgrammeCounterEW (
  input  INCREM,
  input  FINI,
  input  COMMENCER
);

  wire d_ff_1_q, j_k_ff_1_q, j_k_ff_2_q, j_k_ff_3_q, j_k_ff_4_q, undriven;

  D_Flip_Flop d_ff_1 (.D(undriven), .Q(d_ff_1_q));  // open: clk, Qn, preset, reset
  J_K_Flip_Flop j_k_ff_1 (.J(1'b1), .K(d_ff_1_q), .clk(INCREM), .Q(j_k_ff_1_q));  // open: Qn, preset, reset
  T_Flip_Flop t_ff_1 ();  // open: T, clk, Q, Qn, reset, preset
  // OR_Gate or_1 has open pins: in0=FINI, in1=COMMENCER, out=open
  J_K_Flip_Flop j_k_ff_2 (.J(1'b1), .K(1'b1), .clk(j_k_ff_1_q), .Q(j_k_ff_2_q));  // open: Qn, preset, reset
  J_K_Flip_Flop j_k_ff_3 (.J(1'b1), .K(1'b1), .clk(j_k_ff_2_q), .Q(j_k_ff_3_q));  // open: Qn, preset, reset
  J_K_Flip_Flop j_k_ff_4 (.J(1'b1), .K(1'b1), .clk(j_k_ff_3_q), .Q(j_k_ff_4_q));  // open: Qn, preset, reset
endmodule

module test (
  input  in_1,
  input  A0,
  input  A1,
  input  A2,
  input  A3,
  input  OROLOGE,
  input  CMR,
  input  B0,
  input  B1,
  input  B2,
  input  B3,
  input  in_12,
  output out_13,
  output out_14,
  output out_15,
  output out_16
);

  wire controlled_buffer_1_out, controlled_buffer_2_out, d_ff_1_qn, d_ff_2_qn, d_ff_3_qn,
       quatreauncompresseurew_1_a, quatreauncompresseurew_2_a, S0, S1, s_r_ff_1_q;

  D_Flip_Flop d_ff_1 (.D(d_ff_1_qn), .clk(CMR), .Qn(d_ff_1_qn));  // open: Q, preset, reset
  QuatreAUnCompresseurEW quatreauncompresseurew_1 (
    .OROLOGE(OROLOGE), .COMMENCER(CMR), .A0(A0), .A1(A1), .A2(A2), .A3(A3), .FINI(out_13),
    .A(quatreauncompresseurew_1_a));
  QuatreAUnCompresseurEW quatreauncompresseurew_2 (
    .OROLOGE(OROLOGE), .COMMENCER(CMR), .A0(B0), .A1(B1), .A2(B2), .A3(B3), .A(quatreauncompresseurew_2_a));  // open: FINI
  S_R_Flip_Flop s_r_ff_1 (.S(CMR), .R(out_13), .clk(OROLOGE), .Q(s_r_ff_1_q));  // open: reset, Qn, preset
  assign controlled_buffer_1_out = s_r_ff_1_q ? quatreauncompresseurew_1_a : 1'bz;  // Controlled_Buffer controlled_buffer_1
  assign controlled_buffer_2_out = s_r_ff_1_q ? quatreauncompresseurew_2_a : 1'bz;  // Controlled_Buffer controlled_buffer_2
  J_K_Flip_Flop j_k_ff_1 (.J(1'b1), .K(1'b1), .clk(in_1), .Q(S0));  // open: Qn, preset, reset
  OneBitAjoutantEW onebitajoutantew_1 (
    .A(controlled_buffer_1_out), .B(controlled_buffer_2_out), .ACT(s_r_ff_1_q), .K(out_14));  // open: Cin, Cout
  D_Flip_Flop d_ff_2 (.D(d_ff_2_qn), .clk(in_12), .Q(out_15), .Qn(d_ff_2_qn));  // open: preset, reset
  J_K_Flip_Flop j_k_ff_2 (.J(S0), .K(S0), .clk(in_1), .Q(S1));  // open: Qn, preset, reset
  D_Flip_Flop d_ff_3 (.D(d_ff_3_qn), .clk(out_15), .Q(out_16), .Qn(d_ff_3_qn));  // open: preset, reset

  // Other names for the same wires on the sheet: FINI = out_13
endmodule

module test02 (
  input  in_1,
  input  [3:0] A,
  input  [3:0] B,
  input  EN,
  input  CMR,
  input  in_6,
  input  LORG,
  input  in_8,
  input  in_9,
  input  [8:0] in_10,
  output F,
  output OVF,
  output out_13,
  output out_14,
  output out_15,
  output out_16,
  output [3:0] out_17,
  output [3:0] out_18,
  output [3:0] out_19
);

  wire and_1_out, controlled_buffer_1_out, controlled_buffer_2_out, d_ff_2_q, demultiplexer_1_out0,
       demultiplexer_1_out1, demultiplexer_1_out2, demultiplexer_1_out3, multiplexer_1_out,
       multiplexer_2_out, onebitajoutantew_1_cout, onebitajoutantew_1_k, s_r_ff_2_q, s_r_ff_3_q, s_r_ff_4_q,
       s_r_ff_5_q, s_r_ff_6_q;
  wire [1:0] j_k_ff_1_q;

  S_R_Flip_Flop s_r_ff_1 ();  // open: S, R, clk, Q, reset, Qn, preset
  D_Flip_Flop d_ff_1 (.Q(F), .preset(and_1_out));  // open: D, clk, Qn, reset
  Hex_Digit_Display hex_digit_display_1 (.value({2'b00, j_k_ff_1_q}));  // open: dp
  S_R_Flip_Flop s_r_ff_2 (.S(CMR), .R(in_6), .clk(LORG), .Q(s_r_ff_2_q));  // open: reset, Qn, preset
  and and_1 (and_1_out, j_k_ff_1_q[1], j_k_ff_1_q[0]);
  J_K_Flip_Flop j_k_ff_1 (.J(s_r_ff_2_q), .K(s_r_ff_2_q), .clk(LORG), .Q(j_k_ff_1_q[0]));  // open: Qn, preset, reset
  J_K_Flip_Flop j_k_ff_2 (
    .J(j_k_ff_1_q[0]), .K(j_k_ff_1_q[0]), .clk(LORG), .Q(j_k_ff_1_q[1]));  // open: Qn, preset, reset
  Hex_Digit_Display hex_digit_display_2 (.value(out_17));  // open: dp
  // Binary_to_BCD_converter binary_to_bcd_converter_1: pin names not known; wires that end beside it: in_10, out_17, out_18, out_19
  assign controlled_buffer_1_out = EN ? multiplexer_1_out : 1'bz;  // Controlled_Buffer controlled_buffer_1
  Multiplexer #(.select(2)) multiplexer_1 (
    .in0(A[0]), .in1(A[1]), .in2(A[2]), .in3(A[3]), .out(multiplexer_1_out), .sel(j_k_ff_1_q));
  assign controlled_buffer_2_out = EN ? multiplexer_2_out : 1'bz;  // Controlled_Buffer controlled_buffer_2
  Multiplexer #(.select(2)) multiplexer_2 (
    .in0(B[0]), .in1(B[1]), .in2(B[2]), .in3(B[3]), .out(multiplexer_2_out), .sel(j_k_ff_1_q));
  Hex_Digit_Display hex_digit_display_3 (.value(out_18));  // open: dp
  Hex_Digit_Display hex_digit_display_4 (.value(out_19));  // open: dp
  Demultiplexer #(.select(2)) demultiplexer_1 (
    .out0(demultiplexer_1_out0), .out1(demultiplexer_1_out1), .out2(demultiplexer_1_out2),
    .out3(demultiplexer_1_out3), .in(onebitajoutantew_1_k), .sel(j_k_ff_1_q));
  OneBitAjoutantEW onebitajoutantew_1 (
    .A(controlled_buffer_1_out), .B(controlled_buffer_2_out), .Cin(d_ff_2_q), .ACT(EN),
    .K(onebitajoutantew_1_k), .Cout(onebitajoutantew_1_cout));
  D_Flip_Flop d_ff_2 (.D(onebitajoutantew_1_cout), .clk(LORG), .Q(d_ff_2_q));  // open: Qn, preset, reset
  _7_Segment_Display u_7_segment_display_1 ();  // open: g, f, a, b, e, d, c, dp
  S_R_Flip_Flop s_r_ff_3 (.S(demultiplexer_1_out0), .R(in_9), .clk(LORG), .Q(s_r_ff_3_q));  // open: reset, Qn, preset
  S_R_Flip_Flop s_r_ff_4 (.S(demultiplexer_1_out1), .R(in_9), .clk(LORG), .Q(s_r_ff_4_q));  // open: reset, Qn, preset
  S_R_Flip_Flop s_r_ff_5 (.S(demultiplexer_1_out2), .R(in_9), .clk(LORG), .Q(s_r_ff_5_q));  // open: reset, Qn, preset
  S_R_Flip_Flop s_r_ff_6 (.S(demultiplexer_1_out3), .R(in_9), .clk(LORG), .Q(s_r_ff_6_q));  // open: reset, Qn, preset
  assign out_13 = in_8 ? s_r_ff_3_q : 1'bz;  // Controlled_Buffer controlled_buffer_3
  assign out_14 = in_8 ? s_r_ff_4_q : 1'bz;  // Controlled_Buffer controlled_buffer_4
  assign out_15 = in_8 ? s_r_ff_5_q : 1'bz;  // Controlled_Buffer controlled_buffer_5
  assign out_16 = in_8 ? s_r_ff_6_q : 1'bz;  // Controlled_Buffer controlled_buffer_6

  // Notes on the sheet:
  //   status lignes
endmodule

module test03 (
  input  in_1,
  input  LORG,
  input  in_3,
  input  in_4,
  input  in_5,
  input  in_6,
  input  in_7,
  input  in_8
);

  wire and_1_out, controlled_buffer_1_out, d_ff_1_q, d_ff_2_q, d_ff_2_qn, d_ff_3_q, d_ff_3_qn;

  D_Flip_Flop d_ff_1 (.clk(in_5), .Q(d_ff_1_q), .preset(in_3));  // open: D, Qn, reset
  S_R_Flip_Flop s_r_ff_1 (.S(in_6), .R(in_7), .clk(in_8));  // open: Q, reset, Qn, preset
  D_Flip_Flop d_ff_2 (.D(d_ff_2_qn), .clk(and_1_out), .Q(d_ff_2_q), .Qn(d_ff_2_qn));  // open: preset, reset
  and and_1 (and_1_out, in_1, controlled_buffer_1_out);
  assign controlled_buffer_1_out = d_ff_1_q ? LORG : 1'bz;  // Controlled_Buffer controlled_buffer_1
  D_Flip_Flop d_ff_3 (.D(d_ff_3_qn), .clk(d_ff_2_q), .Q(d_ff_3_q), .Qn(d_ff_3_qn), .reset(in_4));  // open: preset

  // Notes on the sheet:
  //   single-délai système
endmodule

module TEST_LoadAjoutant (
  input  in_1,
  input  EN,
  input  CMR,
  input  [3:0] A,
  input  [3:0] B,
  input  LORG,
  output F,
  output OVF
);

  wire and_1_out, controlled_buffer_1_out, controlled_buffer_2_out, d_ff_2_q, multiplexer_1_out,
       multiplexer_2_out, onebitajoutantew_1_cout, onebitajoutantew_1_k, s_r_ff_1_q, undriven;
  wire [1:0] j_k_ff_1_q;

  S_R_Flip_Flop s_r_ff_1 (.S(CMR), .clk(LORG), .Q(s_r_ff_1_q), .reset(undriven));  // open: R, Qn, preset
  D_Flip_Flop d_ff_1 (.Q(F), .preset(and_1_out));  // open: D, clk, Qn, reset
  Hex_Digit_Display hex_digit_display_1 (.value({2'b00, j_k_ff_1_q}));  // open: dp
  J_K_Flip_Flop j_k_ff_1 (
    .J(s_r_ff_1_q), .K(s_r_ff_1_q), .clk(LORG), .Q(j_k_ff_1_q[0]), .reset(undriven));  // open: Qn, preset
  and and_1 (and_1_out, j_k_ff_1_q[1], j_k_ff_1_q[0]);
  J_K_Flip_Flop j_k_ff_2 (
    .J(j_k_ff_1_q[0]), .K(j_k_ff_1_q[0]), .clk(LORG), .Q(j_k_ff_1_q[1]), .reset(undriven));  // open: Qn, preset
  Multiplexer #(.select(2)) multiplexer_1 (
    .in0(A[0]), .in1(A[1]), .in2(A[2]), .in3(A[3]), .out(multiplexer_1_out), .sel(j_k_ff_1_q));
  Multiplexer #(.select(2)) multiplexer_2 (
    .in0(B[0]), .in1(B[1]), .in2(B[2]), .in3(B[3]), .out(multiplexer_2_out), .sel(j_k_ff_1_q));
  assign controlled_buffer_1_out = EN ? multiplexer_1_out : 1'bz;  // Controlled_Buffer controlled_buffer_1
  assign controlled_buffer_2_out = EN ? multiplexer_2_out : 1'bz;  // Controlled_Buffer controlled_buffer_2
  OneBitAjoutantEW onebitajoutantew_1 (
    .A(controlled_buffer_1_out), .B(controlled_buffer_2_out), .Cin(d_ff_2_q), .ACT(EN),
    .K(onebitajoutantew_1_k), .Cout(onebitajoutantew_1_cout));
  D_Flip_Flop d_ff_2 (.D(onebitajoutantew_1_cout), .clk(LORG), .Q(d_ff_2_q));  // open: Qn, preset, reset

  // Notes on the sheet:
  //   CMR et NOUVEAUCOMMAT sont la même
endmodule

module TEST_Incremeneter (
  input  CMR,
  input  LORG,
  input  in_3
);

  wire d_ff_1_q, j_k_ff_1_q;

  D_Flip_Flop d_ff_1 (.Q(d_ff_1_q));  // open: D, clk, Qn, preset, reset
  J_K_Flip_Flop j_k_ff_1 (.J(d_ff_1_q), .K(d_ff_1_q), .clk(LORG), .Q(j_k_ff_1_q));  // open: Qn, preset, reset
  J_K_Flip_Flop j_k_ff_2 (.J(j_k_ff_1_q), .K(j_k_ff_1_q), .clk(LORG));  // open: Q, Qn, preset, reset
  S_R_Flip_Flop s_r_ff_1 ();  // open: S, R, clk, Q, reset, Qn, preset
endmodule
