// Logisim project LivresDesCompsants.circ as structural Verilog
module CPU (
);

  ControllerTEST controllertest_1 ();  // open: LORG_PRIM, INSTRUCTION
  ALU_TEST alu_test_1 ();  // open: LORG_PRIM, LE, EN, FORCE_ARRETER, A, B, OP_CODE, K, FINI, out_11, out_10

  // Notes on the sheet:
  //   instruction register
  //   IO pins
  //   controller
  //   memoire 
  //   (alu_scheduler)
  //   alu
endmodule

module QuatreAUnCompresseurEW (
  input  A0,
  input  A1,
  input  A2,
  input  A3,
  input  OROLOGE,
  input  COMMENCER,
  output FINI,
  output A
);

  wire [1:0] incrementerarchived00_1_s0;

  Multiplexer #(.select(2)) multiplexer_1 (
    .in0(A0), .in1(A1), .in2(A2), .in3(A3), .out(A), .sel(incrementerarchived00_1_s0));
  IncrementerArchived00 incrementerarchived00_1 (
    .OROLOGE(OROLOGE), .COMMENCER(COMMENCER), .FINI(FINI), .S0(incrementerarchived00_1_s0[0]),
    .S1(incrementerarchived00_1_s0[1]));  // open: CMR, in_3, in_1, out_6, out_7

  // Notes on the sheet:
  //   on utilise "fini" bit avec la dernière bit pour minimaliser le delai des components sous-nivel
  //   le delai (pour ejemple un delai d'un cycle peut faire dans les components seuls qu'ont besoin de ça
endmodule

module QuatreAUnCompresseurNS (
  input  A0,
  input  A1,
  input  A2,
  input  A3,
  input  OROLOGE,
  input  COMMENCER,
  output FINI,
  output A
);

  wire [1:0] incrementerarchived00_1_s0;

  Multiplexer #(.select(2)) multiplexer_1 (
    .in0(A0), .in1(A1), .in2(A2), .in3(A3), .out(A), .sel(incrementerarchived00_1_s0));
  IncrementerArchived00 incrementerarchived00_1 (
    .OROLOGE(OROLOGE), .COMMENCER(COMMENCER), .FINI(FINI), .S0(incrementerarchived00_1_s0[0]),
    .S1(incrementerarchived00_1_s0[1]));  // open: CMR, in_3, in_1, out_6, out_7

  // Notes on the sheet:
  //   c'est la même sauf qu'il va du nord au sud
endmodule

module UnAQuatreDecompresseurEW (
  input  OROLOGE,
  input  COMMENCER,
  input  A,
  output FINI,
  output A0,
  output A1,
  output A2,
  output A3
);

  wire [1:0] incrementerarchived01_1_s0;

  IncrementerArchived01 incrementerarchived01_1 (
    .OROLOGE(OROLOGE), .COMMENCER(COMMENCER), .FINI(FINI), .S0(incrementerarchived01_1_s0[0]),
    .S1(incrementerarchived01_1_s0[1]));
  Demultiplexer #(.select(2)) demultiplexer_1 (
    .out0(A0), .out1(A1), .out2(A2), .out3(A3), .in(A), .sel(incrementerarchived01_1_s0));
endmodule

module UnAQuatreDecompresseurNS (
  input  OROLOGE,
  input  COMMENCER,
  input  A,
  output FINI,
  output A0,
  output A1,
  output A2,
  output A3
);

  wire [1:0] incrementerarchived01_1_s0;

  IncrementerArchived01 incrementerarchived01_1 (
    .OROLOGE(OROLOGE), .COMMENCER(COMMENCER), .FINI(FINI), .S0(incrementerarchived01_1_s0[0]),
    .S1(incrementerarchived01_1_s0[1]));
  Demultiplexer #(.select(2)) demultiplexer_1 (
    .out0(A0), .out1(A1), .out2(A2), .out3(A3), .in(A), .sel(incrementerarchived01_1_s0));
endmodule

module IncrementerArchived00 (
  input  in_1,
  input  CMR,
  input  in_3,
  input  OROLOGE,
  input  COMMENCER,
  output out_6,
  output out_7,
  output S0,
  output S1,
  output FINI
);

  wire and_2_out, d_ff_1_q, nand_1_out, or_1_out, t_ff_1_q;

  S_R_Flip_Flop s_r_ff_1 ();  // open: S, R, clk, Q, reset, Qn, preset
  J_K_Flip_Flop j_k_ff_1 (.J(in_1), .K(in_1), .clk(in_3), .Q(out_6));  // open: Qn, preset, reset
  and and_1 (FINI, S1, S0);
  T_Flip_Flop t_ff_1 (.T(or_1_out), .clk(OROLOGE), .Q(t_ff_1_q));  // open: Qn, reset, preset
  or or_1 (or_1_out, FINI, COMMENCER);
  J_K_Flip_Flop j_k_ff_2 (.J(out_6), .K(out_6), .clk(in_3), .Q(out_7));  // open: Qn, preset, reset
  D_Flip_Flop d_ff_1 (.D(nand_1_out), .clk(and_2_out), .Q(d_ff_1_q));  // open: Qn, preset, reset
  and and_2 (and_2_out, OROLOGE, t_ff_1_q);
  J_K_Flip_Flop j_k_ff_3 (.J(d_ff_1_q), .K(d_ff_1_q), .clk(and_2_out), .Q(S0));  // open: Qn, preset, reset
  nand nand_1 (nand_1_out, S0, S1);
  J_K_Flip_Flop j_k_ff_4 (.J(S0), .K(S0), .clk(and_2_out), .Q(S1));  // open: Qn, preset, reset

  // Notes on the sheet:
  //   un formation JK simple, qui utilise un DFF pour un 1-cycle delai
  //   avec ça, il lit 00 pour un temps et n'est pas incrémenter instantement de "00" à "01"
  //   le commencer (cmr) bit peut être activé pour tout le temps petit ou grand
  //   mais, le cmr bit regarde le status pour un cycle trop long
  //   c'est NAND gate fait le 1-temps delai
endmodule

module IncrementerArchived01 (
  input  OROLOGE,
  input  COMMENCER,
  output S0,
  output S1,
  output FINI
);

  wire and_2_out, d_ff_1_q, nand_1_out, or_1_out, t_ff_1_q;

  and and_1 (FINI, S1, S0);
  T_Flip_Flop t_ff_1 (.T(or_1_out), .clk(OROLOGE), .Q(t_ff_1_q));  // open: Qn, reset, preset
  or or_1 (or_1_out, FINI, COMMENCER);
  D_Flip_Flop d_ff_1 (.D(nand_1_out), .clk(and_2_out), .Q(d_ff_1_q));  // open: Qn, preset, reset
  and and_2 (and_2_out, OROLOGE, t_ff_1_q);
  J_K_Flip_Flop j_k_ff_1 (.J(d_ff_1_q), .K(d_ff_1_q), .clk(and_2_out), .Q(S0));  // open: Qn, preset, reset
  nand nand_1 (nand_1_out, S0, S1);
  J_K_Flip_Flop j_k_ff_2 (.J(S0), .K(S0), .clk(and_2_out), .Q(S1));  // open: Qn, preset, reset
endmodule

module OneBitAjoutantFinal (
  input  A,
  input  B,
  input  Cin,
  input  ACT,
  output Cout,
  output K
);

  wire and_1_out, and_2_out, or_1_out, xor_1_out, xor_2_out;

  xor xor_1 (xor_1_out, A, B);
  and and_1 (and_1_out, A, B);
  and and_2 (and_2_out, xor_1_out, Cin);
  xor xor_2 (xor_2_out, xor_1_out, Cin);
  or or_1 (or_1_out, and_1_out, and_2_out);
  and and_3 (K, xor_2_out, ACT);
  and and_4 (Cout, or_1_out, ACT);

  // Notes on the sheet:
  //   1-bit tout ajoutant
  //   L'Inclusion de l'Activer est étrange mais, c'est similaire de "commencer" dans tous autres compsants
endmodule

module OneBitAjoutantArchived00 (
  input  A,
  input  B,
  input  Cin,
  input  ACT,
  output Cout,
  output K
);

  wire and_1_out, and_2_out, or_1_out, xor_1_out, xor_2_out;

  xor xor_1 (xor_1_out, A, B);
  and and_1 (and_1_out, A, B);
  and and_2 (and_2_out, xor_1_out, Cin);
  xor xor_2 (xor_2_out, xor_1_out, Cin);
  or or_1 (or_1_out, and_1_out, and_2_out);
  and and_3 (K, xor_2_out, ACT);
  and and_4 (Cout, or_1_out, ACT);

  // Notes on the sheet:
  //   le NS du tout ajoutant
endmodule

module QuatreBitAjoutantArchived00 (
  input  [3:0] A,
  input  HORG,
  input  CMR,
  input  [3:0] B,
  input  RE,
  input  RST,
  input  Cin,
  output FINI,
  output K0,
  output K1,
  output K2,
  output K3
);

  wire Decompresseur_a, OneBitAjoutant_cout, OneBitAjoutant_k, or_1_out, quatreauncompresseurew_1_a;

  QuatreAUnCompresseurEW Decompresseur (
    .OROLOGE(HORG), .COMMENCER(CMR), .A0(A[0]), .A1(A[1]), .A2(A[2]), .A3(A[3]), .FINI(FINI),
    .A(Decompresseur_a));
  QuatreAUnCompresseurEW quatreauncompresseurew_1 (
    .OROLOGE(HORG), .COMMENCER(CMR), .A0(B[0]), .A1(B[1]), .A2(B[2]), .A3(B[3]),
    .A(quatreauncompresseurew_1_a));  // open: FINI
  or or_1 (or_1_out, Cin, OneBitAjoutant_cout);
  OneBitAjoutantFinal OneBitAjoutant (
    .A(Decompresseur_a), .B(quatreauncompresseurew_1_a), .Cin(or_1_out), .ACT(HORG), .K(OneBitAjoutant_k),
    .Cout(OneBitAjoutant_cout));
  SerialeParalelleRegistreArchived00 Memoire (
    .OROLOGE(HORG), .COMMENCER(CMR), .ENTREE(OneBitAjoutant_k), .RST(RST), .LIRE_ENABLE(RE), .D0(K0),
    .D1(K1), .D2(K2), .D3(K3));  // open: FINI

  // Notes on the sheet:
  //   je ne sais pas la raison que ce truc garde des values et nes autres
  //   ie A = 4, B = 8, fait 12
  //   mais M1 est 1 tous temps, et M2 changer entre 0 et 1
endmodule

module souvenir (
  input  OROLOGE,
  input  COMMENCER,
  input  Entree,
  input  RST,
  output M0,
  output M1,
  output M2,
  output M3
);

  wire d_ff_1_q, d_ff_2_q, d_ff_3_q, d_ff_4_q, demultiplexer_1_out0, demultiplexer_1_out1,
       demultiplexer_1_out2, demultiplexer_1_out3, incrementerarchived01_1_fini, nand_1_out, nand_2_out,
       nand_3_out, nand_4_out, not_1_out, not_2_out;
  wire [1:0] incrementerarchived01_1_s0;

  not not_1 (not_1_out, incrementerarchived01_1_s0[0]);
  not not_2 (not_2_out, incrementerarchived01_1_s0[1]);
  Demultiplexer #(.select(2)) demultiplexer_1 (
    .out0(demultiplexer_1_out0), .out1(demultiplexer_1_out1), .out2(demultiplexer_1_out2),
    .out3(demultiplexer_1_out3), .in(Entree), .sel(incrementerarchived01_1_s0));
  IncrementerArchived01 incrementerarchived01_1 (
    .OROLOGE(OROLOGE), .COMMENCER(COMMENCER), .FINI(incrementerarchived01_1_fini),
    .S0(incrementerarchived01_1_s0[0]), .S1(incrementerarchived01_1_s0[1]));
  D_Flip_Flop #(.trigger("low")) d_ff_1 (
    .D(demultiplexer_1_out0), .clk(nand_1_out), .Q(d_ff_1_q), .reset(RST));  // open: Qn, preset
  nand nand_1 (nand_1_out, not_1_out, not_2_out);
  D_Flip_Flop #(.trigger("low")) d_ff_2 (
    .D(demultiplexer_1_out1), .clk(nand_2_out), .Q(d_ff_2_q), .reset(RST));  // open: Qn, preset
  nand nand_2 (nand_2_out, not_2_out, incrementerarchived01_1_s0[0]);
  D_Flip_Flop #(.trigger("low")) d_ff_3 (
    .D(demultiplexer_1_out2), .clk(nand_3_out), .Q(d_ff_3_q), .reset(RST));  // open: Qn, preset
  nand nand_3 (nand_3_out, incrementerarchived01_1_s0[1], not_1_out);
  D_Flip_Flop #(.trigger("low")) d_ff_4 (
    .D(demultiplexer_1_out3), .clk(nand_4_out), .Q(d_ff_4_q), .reset(RST));  // open: Qn, preset
  nand nand_4 (nand_4_out, incrementerarchived01_1_s0[0], incrementerarchived01_1_s0[1]);
  D_Flip_Flop d_ff_5 (.D(d_ff_1_q), .clk(incrementerarchived01_1_fini), .Q(M0), .reset(RST));  // open: Qn, preset
  D_Flip_Flop d_ff_6 (.D(d_ff_2_q), .clk(incrementerarchived01_1_fini), .Q(M1), .reset(RST));  // open: Qn, preset
  D_Flip_Flop d_ff_7 (.D(d_ff_3_q), .clk(incrementerarchived01_1_fini), .Q(M2), .reset(RST));  // open: Qn, preset
  D_Flip_Flop d_ff_8 (.D(d_ff_4_q), .clk(incrementerarchived01_1_fini), .Q(M3), .reset(RST));  // open: Qn, preset

  // Notes on the sheet:
  //   les choses ci-dessus sont essentiellement un Demux lol 
  //   je les corrigerai plus tard
  //   N'est pas utilisant
  //   M0
  //   M1
  //   M2
  //   M3
  //   4-1 single flush single save unit de mémoire
endmodule

module SerialeParalelleRegistreArchived00 (
  input  ENTREE,
  input  OROLOGE,
  input  COMMENCER,
  input  RST,
  input  LIRE_ENABLE,
  output D0,
  output D1,
  output D2,
  output FINI,
  output D3
);

  wire d_ff_1_q, d_ff_2_q, d_ff_3_q, d_ff_4_q, demultiplexer_1_out0, demultiplexer_1_out1,
       demultiplexer_1_out2, demultiplexer_1_out3, demultiplexer_2_out0, demultiplexer_2_out1,
       demultiplexer_2_out2, demultiplexer_2_out3;
  wire [1:0] incrementerarchived00_1_s0;

  Demultiplexer #(.select(2)) demultiplexer_1 (
    .out0(demultiplexer_1_out0), .out1(demultiplexer_1_out1), .out2(demultiplexer_1_out2),
    .out3(demultiplexer_1_out3), .in(ENTREE), .sel(incrementerarchived00_1_s0));
  Demultiplexer #(.select(2)) demultiplexer_2 (
    .out0(demultiplexer_2_out0), .out1(demultiplexer_2_out1), .out2(demultiplexer_2_out2),
    .out3(demultiplexer_2_out3), .in(1'b1), .sel(incrementerarchived00_1_s0));
  IncrementerArchived00 incrementerarchived00_1 (
    .OROLOGE(OROLOGE), .COMMENCER(COMMENCER), .FINI(FINI), .S0(incrementerarchived00_1_s0[0]),
    .S1(incrementerarchived00_1_s0[1]));  // open: CMR, in_3, in_1, out_6, out_7
  D_Flip_Flop #(.trigger("high")) d_ff_1 (
    .D(demultiplexer_1_out0), .clk(demultiplexer_2_out0), .Q(d_ff_1_q), .reset(RST));  // open: Qn, preset
  D_Flip_Flop d_ff_2 (
    .D(demultiplexer_1_out1), .clk(demultiplexer_2_out1), .Q(d_ff_2_q), .reset(RST));  // open: Qn, preset
  D_Flip_Flop d_ff_3 (
    .D(demultiplexer_1_out2), .clk(demultiplexer_2_out2), .Q(d_ff_3_q), .reset(RST));  // open: Qn, preset
  D_Flip_Flop d_ff_4 (
    .D(demultiplexer_1_out3), .clk(demultiplexer_2_out3), .Q(d_ff_4_q), .reset(RST));  // open: Qn, preset
  assign D0 = LIRE_ENABLE ? d_ff_1_q : 1'bz;  // Controlled_Buffer controlled_buffer_1
  assign D1 = LIRE_ENABLE ? d_ff_2_q : 1'bz;  // Controlled_Buffer controlled_buffer_2
  assign D2 = LIRE_ENABLE ? d_ff_3_q : 1'bz;  // Controlled_Buffer controlled_buffer_3
  assign D3 = LIRE_ENABLE ? d_ff_4_q : 1'bz;  // Controlled_Buffer controlled_buffer_4

  // Notes on the sheet:
  //   utilisant les deux DEMUXs en lieu d'un NAND network
  //   Sériale Entrée -> Paralelle Sortie
  //   4-1 single flush, single save unit de mémoire
endmodule

module ProgrammeCounterEW (
  input  INCREM,
  input  FINI,
  input  COMMENCER
);

  wire d_ff_1_q, j_k_ff_1_q, j_k_ff_2_q, j_k_ff_3_q, j_k_ff_4_q, undriven;

  D_Flip_Flop d_ff_1 (.D(undriven), .Q(d_ff_1_q));  // open: clk, Qn, preset, reset
  J_K_Flip_Flop j_k_ff_1 (.J(1'b1), .K(d_ff_1_q), .clk(INCREM), .Q(j_k_ff_1_q));  // open: Qn, preset, reset
  T_Flip_Flop t_ff_1 ();  // open: T, clk, Q, Qn, reset, preset
  // OR_Gate or_1 has open pins: in0=FINI, in1=COMMENCER, out=open
  J_K_Flip_Flop j_k_ff_2 (.J(1'b1), .K(1'b1), .clk(j_k_ff_1_q), .Q(j_k_ff_2_q));  // open: Qn, preset, reset
  J_K_Flip_Flop j_k_ff_3 (.J(1'b1), .K(1'b1), .clk(j_k_ff_2_q), .Q(j_k_ff_3_q));  // open: Qn, preset, reset
  J_K_Flip_Flop j_k_ff_4 (.J(1'b1), .K(1'b1), .clk(j_k_ff_3_q), .Q(j_k_ff_4_q));  // open: Qn, preset, reset
endmodule

module FourBitAjoutantArchived00 (
  input  in_1,
  input  A0,
  input  A1,
  input  A2,
  input  A3,
  input  OROLOGE,
  input  CMR,
  input  B0,
  input  B1,
  input  B2,
  input  B3,
  input  in_12,
  output out_13,
  output out_14,
  output out_15,
  output out_16
);

  wire controlled_buffer_1_out, controlled_buffer_2_out, d_ff_1_qn, d_ff_2_qn, d_ff_3_qn,
       quatreauncompresseurew_1_a, quatreauncompresseurew_2_a, S0, S1, s_r_ff_1_q;

  D_Flip_Flop d_ff_1 (.D(d_ff_1_qn), .clk(CMR), .Qn(d_ff_1_qn));  // open: Q, preset, reset
  QuatreAUnCompresseurEW quatreauncompresseurew_1 (
    .OROLOGE(OROLOGE), .COMMENCER(CMR), .A0(A0), .A1(A1), .A2(A2), .A3(A3), .FINI(out_13),
    .A(quatreauncompresseurew_1_a));
  QuatreAUnCompresseurEW quatreauncompresseurew_2 (
    .OROLOGE(OROLOGE), .COMMENCER(CMR), .A0(B0), .A1(B1), .A2(B2), .A3(B3), .A(quatreauncompresseurew_2_a));  // open: FINI
  S_R_Flip_Flop s_r_ff_1 (.S(CMR), .R(out_13), .clk(OROLOGE), .Q(s_r_ff_1_q));  // open: reset, Qn, preset
  assign controlled_buffer_1_out = s_r_ff_1_q ? quatreauncompresseurew_1_a : 1'bz;  // Controlled_Buffer controlled_buffer_1
  assign controlled_buffer_2_out = s_r_ff_1_q ? quatreauncompresseurew_2_a : 1'bz;  // Controlled_Buffer controlled_buffer_2
  J_K_Flip_Flop j_k_ff_1 (.J(1'b1), .K(1'b1), .clk(in_1), .Q(S0));  // open: Qn, preset, reset
  OneBitAjoutantFinal onebitajoutantfinal_1 (
    .A(controlled_buffer_1_out), .B(controlled_buffer_2_out), .ACT(s_r_ff_1_q), .K(out_14));  // open: Cin, Cout
  D_Flip_Flop d_ff_2 (.D(d_ff_2_qn), .clk(in_12), .Q(out_15), .Qn(d_ff_2_qn));  // open: preset, reset
  J_K_Flip_Flop j_k_ff_2 (.J(S0), .K(S0), .clk(in_1), .Q(S1));  // open: Qn, preset, reset
  D_Flip_Flop d_ff_3 (.D(d_ff_3_qn), .clk(out_15), .Q(out_16), .Qn(d_ff_3_qn));  // open: preset, reset

  // Other names for the same wires on the sheet: FINI = out_13
endmodule

module FourBitAjoutantArchived01 (
  input  EN,
  input  [3:0] A,
  input  [3:0] B,
  input  CMR,
  input  in_5,
  input  LORG,
  input  in_7,
  input  in_8,
  input  [8:0] in_9,
  output F,
  output OVF,
  output out_12,
  output out_13,
  output out_14,
  output out_15,
  output out_16,
  output [3:0] out_17,
  output [3:0] out_18,
  output [3:0] out_19
);

  wire and_2_out, controlled_buffer_1_out, controlled_buffer_2_out, COUT, d_ff_2_q, demultiplexer_1_out0,
       demultiplexer_1_out1, demultiplexer_1_out2, demultiplexer_1_out3, multiplexer_1_out,
       multiplexer_2_out, onebitajoutantfinal_1_k, s_r_ff_1_q, s_r_ff_2_q, s_r_ff_3_q, s_r_ff_4_q, s_r_ff_5_q;
  wire [1:0] j_k_ff_1_q;

  and and_1 (OVF, COUT, j_k_ff_1_q[1], j_k_ff_1_q[0]);
  D_Flip_Flop d_ff_1 (.Q(F), .preset(and_2_out), .reset(CMR));  // open: D, clk, Qn
  and and_2 (and_2_out, j_k_ff_1_q[1], j_k_ff_1_q[0]);
  Hex_Digit_Display hex_digit_display_1 (.value({2'b00, j_k_ff_1_q}));  // open: dp
  S_R_Flip_Flop s_r_ff_1 (.S(CMR), .R(in_5), .clk(LORG), .Q(s_r_ff_1_q));  // open: reset, Qn, preset
  J_K_Flip_Flop j_k_ff_1 (.J(s_r_ff_1_q), .K(s_r_ff_1_q), .clk(LORG), .Q(j_k_ff_1_q[0]));  // open: Qn, preset, reset
  J_K_Flip_Flop j_k_ff_2 (
    .J(j_k_ff_1_q[0]), .K(j_k_ff_1_q[0]), .clk(LORG), .Q(j_k_ff_1_q[1]));  // open: Qn, preset, reset
  Hex_Digit_Display hex_digit_display_2 (.value(out_17));  // open: dp
  // Binary_to_BCD_converter binary_to_bcd_converter_1: pin names not known; wires that end beside it: COUT, in_9, out_17, out_18, out_19
  assign controlled_buffer_1_out = EN ? multiplexer_1_out : 1'bz;  // Controlled_Buffer controlled_buffer_1
  Multiplexer #(.select(2)) multiplexer_1 (
    .in0(A[0]), .in1(A[1]), .in2(A[2]), .in3(A[3]), .out(multiplexer_1_out), .sel(j_k_ff_1_q));
  assign controlled_buffer_2_out = EN ? multiplexer_2_out : 1'bz;  // Controlled_Buffer controlled_buffer_2
  Multiplexer #(.select(2)) multiplexer_2 (
    .in0(B[0]), .in1(B[1]), .in2(B[2]), .in3(B[3]), .out(multiplexer_2_out), .sel(j_k_ff_1_q));
  Hex_Digit_Display hex_digit_display_3 (.value(out_18));  // open: dp
  Hex_Digit_Display hex_digit_display_4 (.value(out_19));  // open: dp
  Demultiplexer #(.select(2)) demultiplexer_1 (
    .out0(demultiplexer_1_out0), .out1(demultiplexer_1_out1), .out2(demultiplexer_1_out2),
    .out3(demultiplexer_1_out3), .in(onebitajoutantfinal_1_k), .sel(j_k_ff_1_q));
  OneBitAjoutantFinal onebitajoutantfinal_1 (
    .A(controlled_buffer_1_out), .B(controlled_buffer_2_out), .Cin(d_ff_2_q), .ACT(EN),
    .K(onebitajoutantfinal_1_k), .Cout(COUT));
  D_Flip_Flop d_ff_2 (.D(COUT), .clk(LORG), .Q(d_ff_2_q));  // open: Qn, preset, reset
  _7_Segment_Display u_7_segment_display_1 ();  // open: g, f, a, b, e, d, c, dp
  S_R_Flip_Flop s_r_ff_2 (.S(demultiplexer_1_out0), .R(in_8), .clk(LORG), .Q(s_r_ff_2_q));  // open: reset, Qn, preset
  S_R_Flip_Flop s_r_ff_3 (.S(demultiplexer_1_out1), .R(in_8), .clk(LORG), .Q(s_r_ff_3_q));  // open: reset, Qn, preset
  S_R_Flip_Flop s_r_ff_4 (.S(demultiplexer_1_out2), .R(in_8), .clk(LORG), .Q(s_r_ff_4_q));  // open: reset, Qn, preset
  S_R_Flip_Flop s_r_ff_5 (
    .S(demultiplexer_1_out3), .R(in_8), .clk(LORG), .Q(s_r_ff_5_q), .reset(CMR));  // open: Qn, preset
  assign out_13 = in_7 ? s_r_ff_2_q : 1'bz;  // Controlled_Buffer controlled_buffer_3
  assign out_14 = in_7 ? s_r_ff_3_q : 1'bz;  // Controlled_Buffer controlled_buffer_4
  assign out_15 = in_7 ? s_r_ff_4_q : 1'bz;  // Controlled_Buffer controlled_buffer_5
  assign out_16 = in_7 ? s_r_ff_5_q : 1'bz;  // Controlled_Buffer controlled_buffer_6

  // Notes on the sheet:
  //   status lignes
endmodule

module FourBitAjoutantFinal (
  input  LORG,
  input  CMR,
  input  EN,
  input  LE,
  input  RST,
  input  [3:0] A,
  input  [3:0] B,
  output FINI,
  output K0,
  output K1,
  output K2,
  output K3
);

  wire controlled_buffer_1_out, controlled_buffer_2_out, d_ff_1_q, d_ff_2_q, d_ff_3_q, d_ff_4_q, d_ff_5_q,
       demultiplexer_1_out0, demultiplexer_1_out1, demultiplexer_1_out2, demultiplexer_1_out3,
       multiplexer_1_out, multiplexer_2_out, onebitajoutantfinal_1_cout, onebitajoutantfinal_1_k, or_1_out;
  wire [1:0] incrementerfinal_1_val;

  IncrementerFinal incrementerfinal_1 (
    .FORCE_ARRETER(RST), .LORG(LORG), .CMR(CMR), .L1(FINI), .VAL(incrementerfinal_1_val));  // open: L0
  Hex_Digit_Display hex_digit_display_1 (.value({2'b00, incrementerfinal_1_val}));  // open: dp
  Multiplexer #(.select(2)) multiplexer_1 (
    .in0(A[0]), .in1(A[1]), .in2(A[2]), .in3(A[3]), .out(multiplexer_1_out), .sel(incrementerfinal_1_val));
  Multiplexer #(.select(2)) multiplexer_2 (
    .in0(B[0]), .in1(B[1]), .in2(B[2]), .in3(B[3]), .out(multiplexer_2_out), .sel(incrementerfinal_1_val));
  assign controlled_buffer_1_out = EN ? multiplexer_1_out : 1'bz;  // Controlled_Buffer controlled_buffer_1
  assign controlled_buffer_2_out = EN ? multiplexer_2_out : 1'bz;  // Controlled_Buffer controlled_buffer_2
  D_Flip_Flop d_ff_1 (.D(onebitajoutantfinal_1_cout), .clk(LORG), .Q(d_ff_1_q));  // open: Qn, preset, reset
  Demultiplexer #(.select(2)) demultiplexer_1 (
    .out0(demultiplexer_1_out0), .out1(demultiplexer_1_out1), .out2(demultiplexer_1_out2),
    .out3(demultiplexer_1_out3), .in(onebitajoutantfinal_1_k), .sel(incrementerfinal_1_val));
  OneBitAjoutantFinal onebitajoutantfinal_1 (
    .A(controlled_buffer_1_out), .B(controlled_buffer_2_out), .Cin(d_ff_1_q), .ACT(EN),
    .K(onebitajoutantfinal_1_k), .Cout(onebitajoutantfinal_1_cout));
  or or_1 (or_1_out, RST, CMR);
  D_Flip_Flop d_ff_2 (.Q(d_ff_2_q), .preset(demultiplexer_1_out0), .reset(or_1_out));  // open: D, clk, Qn
  D_Flip_Flop d_ff_3 (.Q(d_ff_3_q), .preset(demultiplexer_1_out1), .reset(or_1_out));  // open: D, clk, Qn
  D_Flip_Flop d_ff_4 (.Q(d_ff_4_q), .preset(demultiplexer_1_out2), .reset(or_1_out));  // open: D, clk, Qn
  D_Flip_Flop d_ff_5 (.Q(d_ff_5_q), .preset(demultiplexer_1_out3), .reset(or_1_out));  // open: D, clk, Qn
  assign K0 = LE ? d_ff_2_q : 1'bz;  // Controlled_Buffer controlled_buffer_3
  assign K1 = LE ? d_ff_3_q : 1'bz;  // Controlled_Buffer controlled_buffer_4
  assign K2 = LE ? d_ff_4_q : 1'bz;  // Controlled_Buffer controlled_buffer_5
  assign K3 = LE ? d_ff_5_q : 1'bz;  // Controlled_Buffer controlled_buffer_6
endmodule

module SubtracteurArchived00 (
);

  wire AJT_CMR, and_1_out, and_2_out, F, FORCE_RST, LIRE_A, LORG_PRIM, or_1_out;
  wire [1:0] A_SEL, B_SEL, DEUX_BIT_DEUX;
  wire [2:0] OP_CODE;
  wire [3:0] A_Constant, B_Entree, B_Invert, not_1_out, QUATRE_BIT_ONE;

  or or_1 (or_1_out, FORCE_RST, F);
  and and_1 (and_1_out, OP_CODE[0], ~OP_CODE[1], ~OP_CODE[2], LORG_PRIM);  // AND_Gate
  D_Flip_Flop GARDER_A (.D(and_2_out), .Q(LIRE_A), .preset(and_1_out), .reset(or_1_out));  // open: clk, Qn
  and and_2 (and_2_out, and_1_out, ~LIRE_A);  // AND_Gate
  D_Flip_Flop d_ff_1 (.D(LIRE_A), .clk(LORG_PRIM), .Q(AJT_CMR), .reset(or_1_out));  // open: Qn, preset
  not not_1 (not_1_out[0], B_Entree[0]);
  not not_2 (not_1_out[1], B_Entree[1]);
  not not_3 (not_1_out[2], B_Entree[2]);
  not not_4 (not_1_out[3], B_Entree[3]);
  assign A_Constant = AJT_CMR ? QUATRE_BIT_ONE : 4'bz;  // Controlled_Buffer controlled_buffer_1
  assign A_SEL = AJT_CMR ? DEUX_BIT_DEUX : 2'bz;  // Controlled_Buffer controlled_buffer_2
  assign B_SEL = AJT_CMR ? DEUX_BIT_DEUX : 2'bz;  // Controlled_Buffer controlled_buffer_3
  assign B_Invert = and_1_out ? not_1_out : 4'bz;  // Controlled_Buffer controlled_buffer_4
endmodule

module IncrementerFinal (
  input  FORCE_ARRETER,
  input  LORG,
  input  CMR,
  output L1,
  output L0,
  output [1:0] VAL
);

  wire and_2_out, or_1_out, s_r_ff_1_q, s_r_ff_2_q;

  S_R_Flip_Flop s_r_ff_1 (.S(CMR), .R(1'b0), .clk(LORG), .Q(s_r_ff_1_q), .reset(FORCE_ARRETER));  // open: Qn, preset
  J_K_Flip_Flop j_k_ff_1 (.J(s_r_ff_1_q), .K(s_r_ff_1_q), .clk(LORG), .Q(VAL[0]));  // open: Qn, preset, reset
  J_K_Flip_Flop j_k_ff_2 (.J(VAL[0]), .K(VAL[0]), .clk(LORG), .Q(VAL[1]));  // open: Qn, preset, reset
  Hex_Digit_Display hex_digit_display_1 (.value({2'b00, VAL}));  // open: dp
  and and_1 (L0, VAL[0], VAL[1]);
  and and_2 (and_2_out, VAL[0], VAL[1]);
  S_R_Flip_Flop s_r_ff_2 (
    .S(1'b0), .R(L1), .clk(or_1_out), .Q(s_r_ff_2_q), .reset(CMR), .preset(and_2_out));  // open: Qn
  or or_1 (or_1_out, LORG, L1);
  S_R_Flip_Flop s_r_ff_3 (.S(s_r_ff_2_q), .R(1'b0), .clk(LORG), .Q(L1), .reset(CMR));  // open: Qn, preset

  // Notes on the sheet:
  //   bit0
  //   bit1
  //   latency 0 système
  //   latency 1 système
endmodule

module ALU_testArchived00 (
  input  in_1,
  input  in_2,
  input  EN,
  input  CMR,
  input  [2:0] OP_CODE,
  input  LORG_PRIM,
  input  RST,
  input  [3:0] A,
  input  [3:0] B,
  output out_10,
  output out_11,
  output FINI
);

  wire and_1_out, and_2_out, controlled_buffer_6_out, controlled_buffer_7_out, controlled_buffer_8_out,
       controlled_buffer_9_out, fourbitajoutantfinal_1_k0, fourbitajoutantfinal_1_k1,
       fourbitajoutantfinal_1_k2, fourbitajoutantfinal_1_k3;
  wire [3:0] controlled_buffer_1_out, controlled_buffer_2_out, controlled_buffer_3_out, d_ff_1_q,
       demultiplexer_1_out0, demultiplexer_1_out1, demultiplexer_2_out0, undriven;

  D_Flip_Flop LE_INTERNALE ();  // open: D, clk, Q, Qn, preset, reset
  assign controlled_buffer_1_out = and_2_out ? A : 4'bz;  // Controlled_Buffer controlled_buffer_1
  assign controlled_buffer_2_out = and_2_out ? B : 4'bz;  // Controlled_Buffer controlled_buffer_2
  assign controlled_buffer_3_out = and_1_out ? 4'b0001 : 4'bz;  // Controlled_Buffer controlled_buffer_3
  Demultiplexer #(.select(3), .width(4)) demultiplexer_1 (
    .out0(demultiplexer_1_out0), .out1(demultiplexer_1_out1), .in(controlled_buffer_1_out), .sel(OP_CODE));  // open: out2, out3, out4, out5, out6, out7
  Demultiplexer #(.select(3), .width(4)) demultiplexer_2 (
    .out0(demultiplexer_2_out0), .in(controlled_buffer_2_out), .sel(OP_CODE));  // open: out1, out2, out3, out4, out5, out6, out7
  and and_1 (and_1_out, OP_CODE[0], ~OP_CODE[1], ~OP_CODE[2]);  // AND_Gate
  Demultiplexer demultiplexer_3 (.out0(out_10), .out1(out_11), .in(in_1), .sel(in_2));
  assign controlled_buffer_3_out = and_2_out ? demultiplexer_1_out0 : 4'bz;  // Controlled_Buffer controlled_buffer_4
  assign controlled_buffer_3_out = and_2_out ? demultiplexer_2_out0 : 4'bz;  // Controlled_Buffer controlled_buffer_5
  FourBitAjoutantFinal fourbitajoutantfinal_1 (
    .LORG(LORG_PRIM), .CMR(CMR), .EN(EN), .LE(and_2_out), .RST(RST), .A(controlled_buffer_3_out),
    .B(undriven), .FINI(FINI), .K0(fourbitajoutantfinal_1_k0), .K1(fourbitajoutantfinal_1_k1),
    .K2(fourbitajoutantfinal_1_k2), .K3(fourbitajoutantfinal_1_k3));
  and and_2 (and_2_out, ~OP_CODE[0], ~OP_CODE[1], ~OP_CODE[2]);  // AND_Gate
  assign controlled_buffer_6_out = and_2_out ? fourbitajoutantfinal_1_k0 : 1'bz;  // Controlled_Buffer controlled_buffer_6
  assign controlled_buffer_7_out = and_2_out ? fourbitajoutantfinal_1_k1 : 1'bz;  // Controlled_Buffer controlled_buffer_7
  assign controlled_buffer_8_out = and_2_out ? fourbitajoutantfinal_1_k2 : 1'bz;  // Controlled_Buffer controlled_buffer_8
  assign controlled_buffer_9_out = and_2_out ? fourbitajoutantfinal_1_k3 : 1'bz;  // Controlled_Buffer controlled_buffer_9
  D_Flip_Flop d_ff_1 (.Q(d_ff_1_q[0]), .preset(controlled_buffer_6_out), .reset(RST));  // open: D, clk, Qn
  D_Flip_Flop d_ff_2 (.Q(d_ff_1_q[1]), .preset(controlled_buffer_7_out), .reset(RST));  // open: D, clk, Qn
  D_Flip_Flop d_ff_3 (.Q(d_ff_1_q[2]), .preset(controlled_buffer_8_out), .reset(RST));  // open: D, clk, Qn
  D_Flip_Flop d_ff_4 (.Q(d_ff_1_q[3]), .preset(controlled_buffer_9_out), .reset(RST));  // open: D, clk, Qn

  // Notes on the sheet:
  //   00 - Ajt
  //   01 - Sbt
  //   soft-buffre
  //   non-laminaire flow
endmodule

module ALU_TEST (
  input  LE,
  input  EN,
  input  FORCE_ARRETER,
  input  [3:0] A,
  input  [3:0] B,
  input  LORG_PRIM,
  input  [2:0] OP_CODE,
  output [3:0] K,
  output FINI,
  output [3:0] out_10,
  output [3:0] out_11
);

  wire A_SEL, AJT_CMR, and_1_out, and_2_out, and_3_out, and_4_out, and_5_out, and_6_out, C, d_ff_5_q, LIRE_A,
       LIRE_B;
  wire [2:0] SORTIE_SEL, SRL_SORTIE;
  wire [3:0] A_REG, AJT_SORTIE, B_REG, LOGIQUE_AND, LOGIQUE_OR, multiplexer_1_out, multiplexer_2_out,
       multiplexer_3_out, multiplexer_4_out;
  wire [3:1] SLL_SORTIE;

  and and_1 (and_1_out, ~OP_CODE[0], OP_CODE[1], ~OP_CODE[2], LORG_PRIM);  // AND_Gate
  and and_2 (and_2_out, ~OP_CODE[0], OP_CODE[1], ~OP_CODE[2], LORG_PRIM);  // AND_Gate
  and and_3 (and_3_out, OP_CODE[0], OP_CODE[1], ~OP_CODE[2], LORG_PRIM);  // AND_Gate
  and and_4 (and_4_out, ~OP_CODE[0], ~OP_CODE[1], OP_CODE[2], LORG_PRIM);  // AND_Gate
  and and_5 (and_5_out, OP_CODE[0], ~OP_CODE[1], OP_CODE[2], LORG_PRIM);  // AND_Gate
  D_Flip_Flop d_ff_1 (.clk(LIRE_A), .Q(A_REG[0]), .preset(A[0]), .reset(FORCE_ARRETER));  // open: D, Qn
  D_Flip_Flop d_ff_2 (.clk(LIRE_A), .Q(A_REG[1]), .preset(A[1]), .reset(FORCE_ARRETER));  // open: D, Qn
  D_Flip_Flop d_ff_3 (.clk(LIRE_A), .Q(A_REG[2]), .preset(A[2]), .reset(FORCE_ARRETER));  // open: D, Qn
  D_Flip_Flop d_ff_4 (.clk(LIRE_A), .Q(A_REG[3]), .preset(A[3]), .reset(FORCE_ARRETER));  // open: D, Qn
  and and_6 (and_6_out, ~OP_CODE[0], ~OP_CODE[1], ~OP_CODE[2], LORG_PRIM);  // AND_Gate
  Multiplexer #(.width(4)) multiplexer_1 (.in0(4'b0000), .in1(A), .out(multiplexer_1_out), .sel(and_1_out));
  Multiplexer #(.width(4)) multiplexer_2 (.in0(4'b0000), .in1(B), .out(multiplexer_2_out), .sel(and_1_out));
  Multiplexer #(.width(4)) multiplexer_3 (.in0(4'b0000), .in1(A), .out(multiplexer_3_out), .sel(and_2_out));
  Multiplexer #(.width(4)) multiplexer_4 (.in0(4'b0000), .in1(B), .out(multiplexer_4_out), .sel(and_2_out));
  assign {SRL_SORTIE, C} = and_3_out ? A : 4'bz;  // Controlled_Buffer controlled_buffer_1
  assign {C, SLL_SORTIE} = and_4_out ? A : 4'bz;  // Controlled_Buffer controlled_buffer_2
  assign out_11 = and_5_out ? 4'b0001 : 4'bz;  // Controlled_Buffer controlled_buffer_3
  D_Flip_Flop d_ff_5 (.Q(d_ff_5_q), .preset(and_5_out));  // open: D, clk, Qn, reset
  Multiplexer #(.width(4)) multiplexer_5 (.in0(A), .in1(A_REG), .out(out_10), .sel(A_SEL));
  Multiplexer #(.width(4)) multiplexer_6 (.in0(B), .in1(B_REG), .out(out_11), .sel(A_SEL));
  assign A_SEL = and_6_out ? 1'b0 : 1'bz;  // Controlled_Buffer controlled_buffer_4
  assign AJT_CMR = and_6_out ? 1'b1 : 1'bz;  // Controlled_Buffer controlled_buffer_5
  assign out_10 = and_5_out ? ~A : 4'bz;  // Controlled_Inverter controlled_inverter_1
  assign AJT_CMR = d_ff_5_q ? 1'b1 : 1'bz;  // Controlled_Buffer controlled_buffer_6
  or or_1 (LOGIQUE_OR[0], multiplexer_1_out[0], multiplexer_2_out[0]);
  or or_2 (LOGIQUE_OR[1], multiplexer_1_out[1], multiplexer_2_out[1]);
  or or_3 (LOGIQUE_OR[2], multiplexer_1_out[2], multiplexer_2_out[2]);
  or or_4 (LOGIQUE_OR[3], multiplexer_1_out[3], multiplexer_2_out[3]);
  and and_7 (LOGIQUE_AND[0], multiplexer_3_out[0], multiplexer_4_out[0]);
  and and_8 (LOGIQUE_AND[1], multiplexer_3_out[1], multiplexer_4_out[1]);
  and and_9 (LOGIQUE_AND[2], multiplexer_3_out[2], multiplexer_4_out[2]);
  and and_10 (LOGIQUE_AND[3], multiplexer_3_out[3], multiplexer_4_out[3]);
  D_Flip_Flop d_ff_6 (.D(B[0]), .clk(LIRE_B), .Q(B_REG[0]), .reset(FORCE_ARRETER));  // open: Qn, preset
  D_Flip_Flop d_ff_7 (.D(B[1]), .clk(LIRE_B), .Q(B_REG[1]), .reset(FORCE_ARRETER));  // open: Qn, preset
  D_Flip_Flop d_ff_8 (.D(B[2]), .clk(LIRE_B), .Q(B_REG[2]), .reset(FORCE_ARRETER));  // open: Qn, preset
  D_Flip_Flop d_ff_9 (.D(B[3]), .clk(LIRE_B), .Q(B_REG[3]), .reset(FORCE_ARRETER));  // open: Qn, preset
  assign SORTIE_SEL = and_6_out ? OP_CODE : 3'bz;  // Controlled_Buffer controlled_buffer_7
  assign SORTIE_SEL = and_5_out ? 3'b000 : 3'bz;  // Controlled_Buffer controlled_buffer_8
  assign SORTIE_SEL = and_3_out ? OP_CODE : 3'bz;  // Controlled_Buffer controlled_buffer_9
  assign SORTIE_SEL = and_4_out ? OP_CODE : 3'bz;  // Controlled_Buffer controlled_buffer_10
  Multiplexer #(.select(3), .width(4)) multiplexer_7 (
    .in0(AJT_SORTIE), .in1(LOGIQUE_OR), .in2(LOGIQUE_AND), .in3({1'b0, SRL_SORTIE}),
    .in4({SLL_SORTIE, 1'b0}), .out(K), .sel(SORTIE_SEL));  // open: in5, in6, in7
  FourBitAjoutantFinal fourbitajoutantfinal_1 (
    .LORG(LORG_PRIM), .CMR(AJT_CMR), .EN(EN), .LE(LE), .RST(FORCE_ARRETER), .A(out_10), .B(out_11),
    .FINI(FINI), .K0(AJT_SORTIE[0]), .K1(AJT_SORTIE[1]), .K2(AJT_SORTIE[2]), .K3(AJT_SORTIE[3]));

  // Other names for the same wires on the sheet: A_Entree[3:0] = A; A_t[3:0] = out_10; B_Entree[3:0] = B;
  //   B_SEL = A_SEL; B_t[3:0] = out_11; F = FINI; FORCE_RST = FORCE_ARRETER

  // Notes on the sheet:
  //   il y a besoin d'implémenter le RST
  //   ajt, or, and, srl, sll, 2s, 1s
  //   SEL_LOGIQUE UNIT
  //   car les OR portes ne peuvent pas utiliser moins-X etats
  //   SHIFTER_DROIT_LOGIQUE 011
  //   SHIFTER_GAUCHE_LOGIQUE 100
  //   DEUX_COMP 101
  //   Ajouter 000
  //   LOGIQUE_OR 001
  //   LOGIQUE_AND 010
  //   Ajoutant, Subtracteur, OR Logique, AND Logique, SRL, SLL, 2s Comp, 1s Comp
  //   REGISTRE A
  //   DATA_SEL_LIGNES
  //   DATA_MUXES
  //   REGISTRES
  //   REGISTRE B
  //   CONSTANTS
  //   AJT
endmodule

module ControllerTEST (
  input  LORG_PRIM,
  input  [15:0] INSTRUCTION
);

  wire demultiplexer_1_out0, demultiplexer_1_out1, demultiplexer_1_out2, demultiplexer_1_out3, OUT_REG_EN,
       undriven_2, undriven_3, undriven_4;
  wire [1:0] OUT_REG_SEL, REG_A_SEL, REG_B_SEL, REGISTRE_ADDR_A, REGISTRE_ADDR_B, REGISTRE_ADDR_C;
  wire [2:0] undriven, undriven_5;
  wire [3:0] A, B, demultiplexer_2_out0, demultiplexer_2_out1, demultiplexer_2_out2, demultiplexer_2_out3,
       REG_A, REG_B, REG_DATA, registrefinal_1_s, registrefinal_2_s, registrefinal_3_s, registrefinal_4_s;
  wire [7:0] ADDR;
  wire [15:0] controlled_buffer_4_out;
  wire [15:8] controlled_buffer_5_out;

  Multiplexer #(.select(3), .width(4)) multiplexer_1 (.sel(undriven));  // open: in0, in1, in2, in3, in4, in5, in6, in7, out
  Multiplexer #(.width(2)) multiplexer_2 (.out(REG_A_SEL));  // open: in0, in1, sel
  Controlled_Buffer #(.width(2)) controlled_buffer_1 (.en(undriven_2));  // open: in, out
  Controlled_Buffer #(.width(2)) controlled_buffer_2 (.en(undriven_3));  // open: in, out
  Controlled_Buffer #(.width(2)) controlled_buffer_3 (.en(undriven_4));  // open: in, out
  // AND_Gate and_1 has open pins: in0=INSTRUCTION[12], in1=INSTRUCTION[13], in2=INSTRUCTION[14], in3=INSTRUCTION[15], out=open
  // AND_Gate and_2 has open pins: in0=INSTRUCTION[12], in1=INSTRUCTION[13], in2=INSTRUCTION[14], in3=INSTRUCTION[15], out=open
  // AND_Gate and_3 has open pins: in0=INSTRUCTION[12], in1=INSTRUCTION[13], in2=INSTRUCTION[14], in3=INSTRUCTION[15], out=open
  ALU_TEST alu_test_1 (
    .A(A), .B(B), .OP_CODE(undriven_5), .K(REG_DATA));  // open: LORG_PRIM, LE, EN, FORCE_ARRETER, FINI, out_11, out_10
  assign {controlled_buffer_4_out[15:12], REGISTRE_ADDR_A, REGISTRE_ADDR_B, REGISTRE_ADDR_C, controlled_buffer_4_out[5:0]} = OUT_REG_EN ? INSTRUCTION : 16'bz;  // Controlled_Buffer controlled_buffer_4
  Demultiplexer #(.select(2)) demultiplexer_1 (
    .out0(demultiplexer_1_out0), .out1(demultiplexer_1_out1), .out2(demultiplexer_1_out2),
    .out3(demultiplexer_1_out3), .in(1'b1), .sel(OUT_REG_SEL));
  Demultiplexer #(.select(2), .width(4)) demultiplexer_2 (
    .out0(demultiplexer_2_out0), .out1(demultiplexer_2_out1), .out2(demultiplexer_2_out2),
    .out3(demultiplexer_2_out3), .in(REG_DATA), .sel(OUT_REG_SEL));
  RegistreFinal registrefinal_1 (
    .ENTREE(demultiplexer_2_out0), .ECRIRE(demultiplexer_1_out0), .S(registrefinal_1_s));  // open: FORCE_ARRETER
  RegistreFinal registrefinal_2 (
    .ENTREE(demultiplexer_2_out1), .ECRIRE(demultiplexer_1_out1), .S(registrefinal_2_s));  // open: FORCE_ARRETER
  RegistreFinal registrefinal_3 (
    .ENTREE(demultiplexer_2_out2), .ECRIRE(demultiplexer_1_out2), .S(registrefinal_3_s));  // open: FORCE_ARRETER
  RegistreFinal registrefinal_4 (
    .ENTREE(demultiplexer_2_out3), .ECRIRE(demultiplexer_1_out3), .S(registrefinal_4_s));  // open: FORCE_ARRETER
  assign {controlled_buffer_5_out[15:12], REGISTRE_ADDR_A, controlled_buffer_5_out[9:8], ADDR} = OUT_REG_EN ? INSTRUCTION : 16'bz;  // Controlled_Buffer controlled_buffer_5
  Multiplexer #(.select(2), .width(4)) multiplexer_3 (
    .in0(registrefinal_1_s), .in1(registrefinal_2_s), .in2(registrefinal_3_s), .in3(registrefinal_4_s),
    .out(REG_A), .sel(REG_A_SEL));
  Multiplexer #(.select(2), .width(4)) multiplexer_4 (
    .in0(registrefinal_1_s), .in1(registrefinal_2_s), .in2(registrefinal_3_s), .in3(registrefinal_4_s),
    .out(REG_B), .sel(REG_B_SEL));

  // Other names for the same wires on the sheet: INSTR[15:0] = INSTRUCTION; OP_CODE[3:0] = INSTRUCTION[15:12];
  //   REG_A_ADDR_MODE = OUT_REG_EN; REG_A_REG_MODE = OUT_REG_EN; REG_A_SEL_EN = OUT_REG_EN; REG_B_SEL_EN = OUT_REG_EN

  // Notes on the sheet:
  //   OP_CODE SEL
  //   instruction
  //   SEL_LOG
  //   test du controllre
  //   il y a besoin d'un façon d'accéser les OPCODES
  //   l'instruction va à déterminer l'OPCODE
  //   XXXX 0000 0000 0000
  //   REG_SEL
  //   ex: st r0, 0b00001000
  //   ex: add r0, r1, r2
  //   XXXX 00 00 00 = 4 bit commat, 2 bit registre, 2 bit registre, 2 bit registre = 10 bits
  //   ex: load r0, 0b00010011
  //   XXXX 00 00000000 = 14 bits
  //   instruction = (commat, regA, regB, targetReg)
  //   0000 0000 0000 0000 0000 0000 0000
  //   XXXX 00 00000000 = 4 bit identifier du commat, 2 bit registre, 8 bit location = 14 bits (utiliser 16 bits)
  //   COMMATS:
  //   ADD
  //   ST
  //   INSTRUCTION TEMPLATE
  //   ALU LIGNES
  //   REG_REG
  //   REGISTRES
  //   REG_ADDR
endmodule

module MemoireTEST (
  input  ECRIRE,
  input  LIRE,
  input  MEM_CLAIR,
  input  LORG_PRIM,
  input  EN,
  input  [3:0] DATA,
  input  [7:0] ADDR
);

  wire and_1_out, and_2_out, CS0, CS1, CS2, CS3, ECRIRE_EN, LIRE_EN, UNIT_EN, xor_1_out;

  and and_1 (and_1_out, CS0, LORG_PRIM, UNIT_EN, ECRIRE_EN);
  D_Flip_Flop d_ff_1 (.D(DATA[0]), .clk(and_1_out), .reset(MEM_CLAIR));  // open: Q, Qn, preset
  D_Flip_Flop d_ff_2 (.D(DATA[1]), .reset(MEM_CLAIR));  // open: clk, Q, Qn, preset
  D_Flip_Flop d_ff_3 (.D(DATA[2]), .reset(MEM_CLAIR));  // open: clk, Q, Qn, preset
  D_Flip_Flop d_ff_4 (.D(DATA[3]), .clk(and_1_out), .reset(MEM_CLAIR));  // open: Q, Qn, preset
  assign ECRIRE_EN = xor_1_out ? ECRIRE : 1'bz;  // Controlled_Buffer controlled_buffer_1
  assign LIRE_EN = xor_1_out ? LIRE : 1'bz;  // Controlled_Buffer controlled_buffer_2
  xor xor_1 (xor_1_out, LIRE, ECRIRE);
  and and_2 (and_2_out, LIRE, ECRIRE);
  assign ECRIRE_EN = and_2_out ? ECRIRE : 1'bz;  // Controlled_Buffer controlled_buffer_3
  and and_3 (CS0, ~ADDR[6], EN, ADDR[7]);  // AND_Gate
  and and_4 (CS1, ADDR[6], EN, ADDR[7]);
  and and_5 (CS2, ~ADDR[6], EN, ADDR[7]);  // AND_Gate
  and and_6 (CS3, ADDR[6], EN, ADDR[7]);

  // Notes on the sheet:
  //   UNIT_DE_MÉMOIRE
  //   0-255 addr -> 4 x 64 CS -> A[7:6] = CS
  //   LOGIQUE_MODE
  //   LOGIQUE_CS
endmodule

module test (
  input  B,
  output C
);

  wire clock_1_out;

  Clock clock_1 (.out(clock_1_out));
  and and_1 (C, clock_1_out, B);
endmodule

module RegistreFinal (
  input  [3:0] ENTREE,
  input  ECRIRE,
  input  FORCE_ARRETER,
  output [3:0] S
);

  D_Flip_Flop d_ff_1 (.clk(ECRIRE), .Q(S[0]), .preset(ENTREE[0]), .reset(FORCE_ARRETER));  // open: D, Qn
  D_Flip_Flop d_ff_2 (.clk(ECRIRE), .Q(S[1]), .preset(ENTREE[1]), .reset(FORCE_ARRETER));  // open: D, Qn
  D_Flip_Flop d_ff_3 (.clk(ECRIRE), .Q(S[2]), .preset(ENTREE[2]), .reset(FORCE_ARRETER));  // open: D, Qn
  D_Flip_Flop d_ff_4 (.clk(ECRIRE), .Q(S[3]), .preset(ENTREE[3]), .reset(FORCE_ARRETER));  // open: D, Qn

  // Notes on the sheet:
  //   REGISTRE
endmodule
