// Logisim project ChesapeakeArchitectureBlocks.circ as structural Verilog: 5 circuits, main circuit toplevel
module toplevel (
  input  [31:0] in_1,
  input  clk
);

  wire controller_1_ir_write, controller_1_pc_write;
  wire [1:0] controller_1_alu_src_a, controller_1_ir_source, controller_1_pc_source;
  wire [2:0] controller_1_alu_src_b;
  wire [4:0] undriven_2;
  wire [6:0] undriven_3;
  wire [31:0] alu_1_x, ir_reg_q, memory_1_data_out, multiplexer_1_out, multiplexer_2_out, multiplexer_3_out,
       multiplexer_4_out, multiplexer_5_out, pc_q, reg_a_q, regfile_outdata1, regfile_outdata2, undriven;

  Register #(.width(32)) pc (.D(multiplexer_1_out), .en(controller_1_pc_write), .Q(pc_q));  // open: clk, clr
  Multiplexer #(.select(2), .width(32)) multiplexer_1 (
    .in0(ir_reg_q), .out(multiplexer_1_out), .sel(controller_1_pc_source));  // open: in1, in2, in3
  Multiplexer #(.select(2), .width(32)) multiplexer_2 (
    .in0(pc_q), .out(multiplexer_2_out));  // open: in1, in2, in3, sel
  memory memory_1 (
    .addr(multiplexer_2_out), .data_out(memory_1_data_out));  // open: sw_arr, button0, butotn1, button2, button3, data_in, wr_en, clk, rst, led0, led1, led2, led3, led4, led5, led6, led7
  Multiplexer #(.select(2), .width(32)) multiplexer_3 (
    .in0(memory_1_data_out), .out(multiplexer_3_out), .sel(controller_1_ir_source));  // open: in1, in2, in3
  Register #(.width(32)) ir_reg (
    .D(multiplexer_3_out), .en(controller_1_ir_write), .clk(clk), .Q(ir_reg_q));  // open: clr
  controller controller_1 (
    .ir_31_0(ir_reg_q), .alu_src_a(controller_1_alu_src_a), .alu_src_b(controller_1_alu_src_b),
    .ir_write(controller_1_ir_write), .ir_source(controller_1_ir_source), .pc_source(controller_1_pc_source),
    .pc_write(controller_1_pc_write));  // open: in_2, in_3, in_4, in_5, in_6, in_7
  registerfile regfile (
    .outdata1(regfile_outdata1), .outdata2(regfile_outdata2));  // open: regaddr1, regaddr2, wrdata1, wrdata2, rdwr_config, link_reg, clk
  Multiplexer #(.select(2), .width(32)) multiplexer_4 (
    .in0(regfile_outdata1), .out(multiplexer_4_out), .sel(controller_1_alu_src_a));  // open: in1, in2, in3
  Multiplexer #(.select(3), .width(32)) multiplexer_5 (
    .in0(regfile_outdata2), .out(multiplexer_5_out), .sel(controller_1_alu_src_b));  // open: in1, in2, in3, in4, in5, in6, in7
  Register #(.width(32)) reg_a (.D(multiplexer_4_out), .Q(reg_a_q));  // open: en, clk, clr
  Register #(.width(32)) reg_b (.D(multiplexer_5_out));  // open: en, clk, Q, clr
  ALU alu_1 (.A(reg_a_q), .B(undriven), .shamt(undriven_2), .op(undriven_3), .X(alu_1_x));

  // Notes on the sheet:
  //   i-type
  //   s-type
  //   b-type
  //   u-type
  //   j-type
  //   j-type 2
endmodule

module controller (
  input  [31:0] ir_31_0,
  input  [1:0] in_2,
  input  [2:0] in_3,
  input  in_4,
  input  [1:0] in_5,
  input  [1:0] in_6,
  input  in_7,
  output [1:0] alu_src_a,
  output [2:0] alu_src_b,
  output ir_write,
  output [1:0] ir_source,
  output [1:0] pc_source,
  output pc_write
);


  assign alu_src_a = in_2;
  assign alu_src_b = in_3;
  assign ir_source = in_5;
  assign ir_write = in_4;
  assign pc_source = in_6;
  assign pc_write = in_7;
endmodule

module registerfile (
  input  [4:0] regaddr1,
  input  [4:0] regaddr2,
  input  [31:0] wrdata1,
  input  [31:0] wrdata2,
  input  [1:0] rdwr_config,
  input  link_reg,
  input  clk,
  output [31:0] outdata1,
  output [31:0] outdata2
);
endmodule

module ALU (
  input  [31:0] A,
  input  [31:0] B,
  input  [4:0] shamt,
  input  [6:0] op,
  output [31:0] X
);


  assign X = {32{1'b0}};
endmodule

module memory (
  input  [31:0] addr,
  input  [31:0] data_in,
  input  wr_en,
  input  clk,
  input  rst,
  input  [15:0] sw_arr,
  input  button0,
  input  butotn1,
  input  button2,
  input  button3,
  output [31:0] data_out,
  output [6:0] led0,
  output [6:0] led1,
  output [6:0] led2,
  output [6:0] led3,
  output [6:0] led4,
  output [6:0] led5,
  output [6:0] led6,
  output [6:0] led7
);
endmodule
